// Logisim project control_logic.circ as structural Verilog: 1 circuit, main circuit control_logic
module control_logic (
  input  [31:0] inst,
  input  BrEq,
  input  BrLt,
  output PCSel,
  output RegWEn,
  output [2:0] ImmSel,
  output BrUn,
  output ASel,
  output BSel,
  output [3:0] ALUSel,
  output MemRW,
  output [1:0] WBSel,
  output CSRSel,
  output CSRWen
);

  wire and_1_out, and_3_out, and_4_out, and_5_out, and_6_out, and_7_out, and_8_out, and_9_out, and_10_out,
       and_11_out, and_12_out, and_13_out, and_14_out, and_15_out, and_16_out, and_17_out, and_18_out,
       and_19_out, and_21_out, and_22_out, and_23_out, and_24_out, and_25_out, and_26_out, and_27_out,
       and_28_out, and_29_out, and_30_out, and_31_out, and_32_out, and_33_out, and_34_out, and_35_out,
       comparator_1_eq, comparator_2_eq, comparator_3_eq, comparator_4_eq, comparator_5_eq, comparator_6_eq,
       comparator_7_eq, comparator_8_eq, comparator_9_eq, comparator_10_eq, comparator_11_eq,
       comparator_13_eq, comparator_14_eq, comparator_15_eq, comparator_16_eq, comparator_17_eq,
       comparator_18_eq, comparator_19_eq, comparator_20_eq, comparator_21_eq, comparator_22_eq,
       comparator_23_eq, comparator_24_eq, comparator_25_eq, comparator_26_eq, comparator_27_eq,
       comparator_28_eq, comparator_29_eq, comparator_30_eq, comparator_31_eq, comparator_32_eq,
       comparator_33_eq, comparator_34_eq, comparator_35_eq, comparator_36_eq, comparator_37_eq,
       comparator_38_eq, comparator_39_eq, comparator_40_eq, comparator_41_eq, comparator_42_eq,
       comparator_43_eq, comparator_44_eq, comparator_45_eq, comparator_46_eq, comparator_47_eq,
       comparator_48_eq, comparator_49_eq, comparator_50_eq, comparator_51_eq, comparator_52_eq,
       comparator_53_eq, comparator_54_eq, comparator_55_eq, comparator_56_eq, comparator_57_eq,
       comparator_58_eq, comparator_59_eq, comparator_60_eq, comparator_62_eq, comparator_63_eq,
       comparator_64_eq, comparator_65_eq, comparator_66_eq, comparator_67_eq, comparator_68_eq, not_2_out,
       not_3_out, not_4_out, or_1_out;
  wire [1:0] adder_1_out, adder_3_out, adder_4_out, bit_extender_1_out, bit_extender_2_out,
       bit_extender_3_out, bit_extender_4_out, bit_extender_5_out, multiplier_1_out;
  wire [2:0] adder_5_out, adder_6_out, adder_7_out, adder_8_out, adder_9_out, adder_10_out, adder_11_out,
       bit_extender_6_out, bit_extender_7_out, bit_extender_8_out, bit_extender_9_out, bit_extender_10_out,
       bit_extender_11_out, bit_extender_12_out, bit_extender_13_out, bit_extender_14_out, multiplier_2_out,
       multiplier_3_out, multiplier_4_out, multiplier_5_out, multiplier_6_out, multiplier_7_out,
       multiplier_8_out, multiplier_9_out, multiplier_10_out;
  wire [3:0] adder_13_out, adder_14_out, adder_15_out, adder_16_out, adder_17_out, adder_18_out,
       adder_19_out, adder_20_out, adder_22_out, adder_23_out, adder_24_out, adder_25_out, adder_26_out,
       adder_27_out, adder_28_out, adder_29_out, adder_30_out, adder_31_out, adder_32_out,
       bit_extender_15_out, bit_extender_16_out, bit_extender_17_out, bit_extender_18_out,
       bit_extender_19_out, bit_extender_20_out, bit_extender_21_out, bit_extender_22_out,
       bit_extender_23_out, bit_extender_24_out, bit_extender_25_out, bit_extender_26_out,
       bit_extender_27_out, bit_extender_28_out, bit_extender_29_out, bit_extender_30_out,
       bit_extender_31_out, bit_extender_32_out, bit_extender_33_out, bit_extender_34_out,
       bit_extender_35_out, multiplier_11_out, multiplier_12_out, multiplier_13_out, multiplier_14_out,
       multiplier_15_out, multiplier_16_out, multiplier_17_out, multiplier_18_out, multiplier_19_out,
       multiplier_20_out, multiplier_21_out, multiplier_22_out, multiplier_23_out, multiplier_24_out,
       multiplier_25_out, multiplier_26_out, multiplier_27_out, multiplier_28_out, multiplier_29_out,
       multiplier_30_out, multiplier_31_out;

  Comparator #(.width(3)) comparator_1 (.a(inst[14:12]), .b(3'b110), .eq(comparator_1_eq));  // open: gt, lt
  Comparator #(.width(3)) comparator_2 (.a(inst[14:12]), .b(3'b111), .eq(comparator_2_eq));  // open: gt, lt
  Comparator #(.width(7)) comparator_3 (.a(inst[6:0]), .b(7'b0110011), .eq(comparator_3_eq));  // open: gt, lt
  Comparator #(.width(7)) comparator_4 (.a(inst[6:0]), .b(7'b0000011), .eq(comparator_4_eq));  // open: gt, lt
  Comparator #(.width(7)) comparator_5 (.a(inst[6:0]), .b(7'b0010011), .eq(comparator_5_eq));  // open: gt, lt
  Comparator #(.width(7)) comparator_6 (.a(inst[6:0]), .b(7'b1100111), .eq(comparator_6_eq));  // open: gt, lt
  Comparator #(.width(7)) comparator_7 (.a(inst[6:0]), .b(7'b1110011), .eq(comparator_7_eq));  // open: gt, lt
  Comparator #(.width(7)) comparator_8 (.a(inst[6:0]), .b(7'b0010111), .eq(comparator_8_eq));  // open: gt, lt
  Comparator #(.width(7)) comparator_9 (.a(inst[6:0]), .b(7'b0110111), .eq(comparator_9_eq));  // open: gt, lt
  Comparator #(.width(7)) comparator_10 (.a(inst[6:0]), .b(7'b1101111), .eq(comparator_10_eq));  // open: gt, lt
  Comparator #(.width(7)) comparator_11 (.a(inst[6:0]), .b(7'b1100011), .eq(comparator_11_eq));  // open: gt, lt
  Comparator #(.width(7)) comparator_12 (.a(inst[6:0]), .b(7'b0100011), .eq(MemRW));  // open: gt, lt
  Comparator #(.width(7)) comparator_13 (.a(inst[6:0]), .b(7'b0110011), .eq(comparator_13_eq));  // open: gt, lt
  Comparator #(.width(7)) comparator_14 (.a(inst[6:0]), .b(7'b1100011), .eq(comparator_14_eq));  // open: gt, lt
  Comparator #(.width(7)) comparator_15 (.a(inst[6:0]), .b(7'b1110011), .eq(comparator_15_eq));  // open: gt, lt
  Comparator #(.width(3)) comparator_16 (.a(inst[14:12]), .b(3'b011), .eq(comparator_16_eq));  // open: gt, lt
  Comparator #(.width(7)) comparator_17 (.a(inst[6:0]), .b(7'b0010111), .eq(comparator_17_eq));  // open: gt, lt
  Comparator #(.width(7)) comparator_18 (.a(inst[6:0]), .b(7'b0110111), .eq(comparator_18_eq));  // open: gt, lt
  Comparator #(.width(7)) comparator_19 (.a(inst[6:0]), .b(7'b1101111), .eq(comparator_19_eq));  // open: gt, lt
  not not_1 (BSel, comparator_13_eq);
  Comparator #(.width(7)) comparator_20 (.a(inst[6:0]), .b(7'b0110011), .eq(comparator_20_eq));  // open: gt, lt
  Comparator #(.width(7)) comparator_21 (.a(inst[6:0]), .b(7'b0000011), .eq(comparator_21_eq));  // open: gt, lt
  Comparator #(.width(7)) comparator_22 (.a(inst[6:0]), .b(7'b0010011), .eq(comparator_22_eq));  // open: gt, lt
  Comparator #(.width(7)) comparator_23 (.a(inst[6:0]), .b(7'b0010111), .eq(comparator_23_eq));  // open: gt, lt
  Comparator #(.width(7)) comparator_24 (.a(inst[6:0]), .b(7'b0110111), .eq(comparator_24_eq));  // open: gt, lt
  or or_1 (or_1_out, comparator_1_eq, comparator_2_eq);
  assign bit_extender_1_out = {{1{1'b0}}, comparator_20_eq};  // Bit_Extender bit_extender_1
  assign bit_extender_2_out = {{1{1'b0}}, comparator_21_eq};  // Bit_Extender bit_extender_2
  assign bit_extender_3_out = {{1{1'b0}}, comparator_22_eq};  // Bit_Extender bit_extender_3
  assign bit_extender_4_out = {{1{1'b0}}, comparator_23_eq};  // Bit_Extender bit_extender_4
  assign bit_extender_5_out = {{1{1'b0}}, comparator_24_eq};  // Bit_Extender bit_extender_5
  or or_2 (RegWEn, comparator_3_eq, comparator_4_eq, comparator_5_eq, comparator_6_eq, comparator_7_eq, comparator_8_eq, comparator_9_eq, comparator_10_eq);
  and and_1 (and_1_out, comparator_15_eq, comparator_16_eq);
  Multiplier #(.width(2)) multiplier_1 (.a(bit_extender_2_out), .b(2'b10), .out(multiplier_1_out));  // open: cin, cout
  Adder #(.width(2)) adder_1 (.a(adder_4_out), .b(bit_extender_4_out), .out(adder_1_out));  // open: cin, cout
  Adder #(.width(2)) adder_2 (.a(adder_1_out), .b(bit_extender_5_out), .out(WBSel));  // open: cin, cout
  and and_2 (BrUn, comparator_11_eq, or_1_out);
  Adder #(.width(2)) adder_3 (.a(bit_extender_1_out), .b(multiplier_1_out), .out(adder_3_out));  // open: cin, cout
  Adder #(.width(2)) adder_4 (.a(adder_3_out), .b(bit_extender_3_out), .out(adder_4_out));  // open: cin, cout
  or or_3 (ASel, comparator_14_eq, and_1_out, comparator_17_eq, comparator_18_eq, comparator_19_eq);
  Comparator #(.width(7)) comparator_25 (.a(inst[6:0]), .b(7'b0000011), .eq(comparator_25_eq));  // open: gt, lt
  Comparator #(.width(7)) comparator_26 (.a(inst[6:0]), .b(7'b0010011), .eq(comparator_26_eq));  // open: gt, lt
  Comparator #(.width(7)) comparator_27 (.a(inst[6:0]), .b(7'b1100111), .eq(comparator_27_eq));  // open: gt, lt
  Comparator #(.width(7)) comparator_28 (.a(inst[6:0]), .b(7'b1110011), .eq(comparator_28_eq));  // open: gt, lt
  Comparator #(.width(7)) comparator_29 (.a(inst[6:0]), .b(7'b0100011), .eq(comparator_29_eq));  // open: gt, lt
  Comparator #(.width(7)) comparator_30 (.a(inst[6:0]), .b(7'b1100011), .eq(comparator_30_eq));  // open: gt, lt
  Comparator #(.width(7)) comparator_31 (.a(inst[6:0]), .b(7'b0010111), .eq(comparator_31_eq));  // open: gt, lt
  Comparator #(.width(7)) comparator_32 (.a(inst[6:0]), .b(7'b0110111), .eq(comparator_32_eq));  // open: gt, lt
  Comparator #(.width(7)) comparator_33 (.a(inst[6:0]), .b(7'b1101111), .eq(comparator_33_eq));  // open: gt, lt
  Comparator #(.width(7)) comparator_34 (.a(inst[6:0]), .b(7'b1100011), .eq(comparator_34_eq));  // open: gt, lt
  Comparator #(.width(7)) comparator_35 (.a(inst[6:0]), .b(7'b1100111), .eq(comparator_35_eq));  // open: gt, lt
  Comparator #(.width(7)) comparator_36 (.a(inst[6:0]), .b(7'b1101111), .eq(comparator_36_eq));  // open: gt, lt
  assign bit_extender_6_out = {{2{1'b0}}, comparator_25_eq};  // Bit_Extender bit_extender_6
  assign bit_extender_7_out = {{2{1'b0}}, comparator_26_eq};  // Bit_Extender bit_extender_7
  assign bit_extender_8_out = {{2{1'b0}}, comparator_27_eq};  // Bit_Extender bit_extender_8
  assign bit_extender_9_out = {{2{1'b0}}, comparator_28_eq};  // Bit_Extender bit_extender_9
  assign bit_extender_10_out = {{2{1'b0}}, comparator_29_eq};  // Bit_Extender bit_extender_10
  assign bit_extender_11_out = {{2{1'b0}}, comparator_30_eq};  // Bit_Extender bit_extender_11
  assign bit_extender_12_out = {{2{1'b0}}, comparator_31_eq};  // Bit_Extender bit_extender_12
  assign bit_extender_13_out = {{2{1'b0}}, comparator_32_eq};  // Bit_Extender bit_extender_13
  assign bit_extender_14_out = {{2{1'b0}}, comparator_33_eq};  // Bit_Extender bit_extender_14
  Comparator #(.width(3)) comparator_37 (.a(inst[14:12]), .b(3'b000), .eq(comparator_37_eq));  // open: gt, lt
  Comparator #(.width(3)) comparator_38 (.a(inst[14:12]), .b(3'b001), .eq(comparator_38_eq));  // open: gt, lt
  Comparator #(.width(3)) comparator_39 (.a(inst[14:12]), .b(3'b100), .eq(comparator_39_eq));  // open: gt, lt
  Comparator #(.width(3)) comparator_40 (.a(inst[14:12]), .b(3'b101), .eq(comparator_40_eq));  // open: gt, lt
  Comparator #(.width(3)) comparator_41 (.a(inst[14:12]), .b(3'b110), .eq(comparator_41_eq));  // open: gt, lt
  Comparator #(.width(3)) comparator_42 (.a(inst[14:12]), .b(3'b111), .eq(comparator_42_eq));  // open: gt, lt
  Comparator #(.width(7)) comparator_43 (.a(inst[6:0]), .b(7'b0110011), .eq(comparator_43_eq));  // open: gt, lt
  Comparator #(.width(3)) comparator_44 (.a(inst[14:12]), .b(3'b000), .eq(comparator_44_eq));  // open: gt, lt
  Comparator #(.width(3)) comparator_45 (.a(inst[14:12]), .b(3'b001), .eq(comparator_45_eq));  // open: gt, lt
  Comparator #(.width(3)) comparator_46 (.a(inst[14:12]), .b(3'b010), .eq(comparator_46_eq));  // open: gt, lt
  Comparator #(.width(3)) comparator_47 (.a(inst[14:12]), .b(3'b011), .eq(comparator_47_eq));  // open: gt, lt
  Comparator #(.width(3)) comparator_48 (.a(inst[14:12]), .b(3'b100), .eq(comparator_48_eq));  // open: gt, lt
  Comparator #(.width(3)) comparator_49 (.a(inst[14:12]), .b(3'b101), .eq(comparator_49_eq));  // open: gt, lt
  Comparator #(.width(3)) comparator_50 (.a(inst[14:12]), .b(3'b110), .eq(comparator_50_eq));  // open: gt, lt
  Comparator #(.width(3)) comparator_51 (.a(inst[14:12]), .b(3'b111), .eq(comparator_51_eq));  // open: gt, lt
  Comparator #(.width(7)) comparator_52 (.a(inst[6:0]), .b(7'b0010011), .eq(comparator_52_eq));  // open: gt, lt
  Comparator #(.width(3)) comparator_53 (.a(inst[14:12]), .b(3'b000), .eq(comparator_53_eq));  // open: gt, lt
  Comparator #(.width(3)) comparator_54 (.a(inst[14:12]), .b(3'b001), .eq(comparator_54_eq));  // open: gt, lt
  Comparator #(.width(3)) comparator_55 (.a(inst[14:12]), .b(3'b010), .eq(comparator_55_eq));  // open: gt, lt
  Comparator #(.width(3)) comparator_56 (.a(inst[14:12]), .b(3'b100), .eq(comparator_56_eq));  // open: gt, lt
  Comparator #(.width(3)) comparator_57 (.a(inst[14:12]), .b(3'b101), .eq(comparator_57_eq));  // open: gt, lt
  Comparator #(.width(3)) comparator_58 (.a(inst[14:12]), .b(3'b110), .eq(comparator_58_eq));  // open: gt, lt
  Comparator #(.width(3)) comparator_59 (.a(inst[14:12]), .b(3'b111), .eq(comparator_59_eq));  // open: gt, lt
  Comparator #(.width(7)) comparator_60 (.a(inst[6:0]), .b(7'b0110111), .eq(comparator_60_eq));  // open: gt, lt
  Multiplier #(.width(3)) multiplier_2 (.a(bit_extender_6_out), .b(3'b010), .out(multiplier_2_out));  // open: cin, cout
  Multiplier #(.width(3)) multiplier_3 (.a(bit_extender_7_out), .b(3'b010), .out(multiplier_3_out));  // open: cin, cout
  assign bit_extender_15_out = {{3{1'b0}}, comparator_60_eq};  // Bit_Extender bit_extender_15
  Multiplier #(.width(3)) multiplier_4 (.a(bit_extender_8_out), .b(3'b010), .out(multiplier_4_out));  // open: cin, cout
  Multiplier #(.width(3)) multiplier_5 (.a(bit_extender_9_out), .b(3'b010), .out(multiplier_5_out));  // open: cin, cout
  Multiplier #(.width(3)) multiplier_6 (
    .a(bit_extender_10_out), .b(3'b011), .out(multiplier_6_out));  // open: cin, cout
  Multiplier #(.width(3)) multiplier_7 (
    .a(bit_extender_11_out), .b(3'b100), .out(multiplier_7_out));  // open: cin, cout
  Multiplier #(.width(3)) multiplier_8 (
    .a(bit_extender_12_out), .b(3'b101), .out(multiplier_8_out));  // open: cin, cout
  Multiplier #(.width(3)) multiplier_9 (
    .a(bit_extender_13_out), .b(3'b101), .out(multiplier_9_out));  // open: cin, cout
  Multiplier #(.width(3)) multiplier_10 (
    .a(bit_extender_14_out), .b(3'b110), .out(multiplier_10_out));  // open: cin, cout
  Comparator #(.width(7)) comparator_61 (.a(inst[6:0]), .b(7'b1110011), .eq(CSRWen));  // open: gt, lt
  Comparator #(.width(7)) comparator_62 (.a(inst[6:0]), .b(7'b1110011), .eq(comparator_62_eq));  // open: gt, lt
  Comparator #(.width(3)) comparator_63 (.a(inst[14:12]), .b(3'b101), .eq(comparator_63_eq));  // open: gt, lt
  Adder #(.width(3)) adder_5 (.a(multiplier_2_out), .b(multiplier_3_out), .out(adder_5_out));  // open: cin, cout
  Adder #(.width(3)) adder_6 (.a(adder_5_out), .b(multiplier_4_out), .out(adder_6_out));  // open: cin, cout
  Adder #(.width(3)) adder_7 (.a(adder_6_out), .b(multiplier_5_out), .out(adder_7_out));  // open: cin, cout
  Adder #(.width(3)) adder_8 (.a(adder_7_out), .b(multiplier_6_out), .out(adder_8_out));  // open: cin, cout
  Adder #(.width(3)) adder_9 (.a(adder_8_out), .b(multiplier_7_out), .out(adder_9_out));  // open: cin, cout
  Adder #(.width(3)) adder_10 (.a(adder_9_out), .b(multiplier_8_out), .out(adder_10_out));  // open: cin, cout
  Adder #(.width(3)) adder_11 (.a(adder_10_out), .b(multiplier_9_out), .out(adder_11_out));  // open: cin, cout
  Adder #(.width(3)) adder_12 (.a(adder_11_out), .b(multiplier_10_out), .out(ImmSel));  // open: cin, cout
  and and_3 (and_3_out, comparator_34_eq, comparator_37_eq);
  and and_4 (and_4_out, comparator_34_eq, comparator_38_eq);
  and and_5 (and_5_out, comparator_34_eq, comparator_39_eq);
  and and_6 (and_6_out, comparator_34_eq, comparator_40_eq);
  and and_7 (and_7_out, comparator_34_eq, comparator_41_eq);
  and and_8 (and_8_out, comparator_34_eq, comparator_42_eq);
  and and_9 (and_9_out, comparator_43_eq, comparator_46_eq);
  and and_10 (and_10_out, comparator_43_eq, comparator_47_eq);
  and and_11 (and_11_out, comparator_43_eq, comparator_48_eq);
  and and_12 (and_12_out, comparator_43_eq, comparator_50_eq);
  and and_13 (and_13_out, comparator_43_eq, comparator_51_eq);
  and and_14 (and_14_out, comparator_52_eq, comparator_53_eq);
  and and_15 (and_15_out, comparator_52_eq, comparator_54_eq);
  and and_16 (and_16_out, comparator_52_eq, comparator_55_eq);
  and and_17 (and_17_out, comparator_52_eq, comparator_56_eq);
  and and_18 (and_18_out, comparator_52_eq, comparator_58_eq);
  and and_19 (and_19_out, comparator_52_eq, comparator_59_eq);
  not not_2 (not_2_out, BrEq);
  not not_3 (not_3_out, BrLt);
  not not_4 (not_4_out, BrLt);
  assign bit_extender_16_out = {{3{1'b0}}, and_12_out};  // Bit_Extender bit_extender_16
  assign bit_extender_17_out = {{3{1'b0}}, and_13_out};  // Bit_Extender bit_extender_17
  assign bit_extender_18_out = {{3{1'b0}}, and_18_out};  // Bit_Extender bit_extender_18
  assign bit_extender_19_out = {{3{1'b0}}, and_19_out};  // Bit_Extender bit_extender_19
  Multiplier #(.width(4)) multiplier_11 (
    .a(bit_extender_15_out), .b(4'b1101), .out(multiplier_11_out));  // open: cin, cout
  and and_20 (CSRSel, comparator_62_eq, comparator_63_eq);
  and and_21 (and_21_out, and_7_out, BrLt);
  assign bit_extender_20_out = {{3{1'b0}}, and_14_out};  // Bit_Extender bit_extender_20
  assign bit_extender_21_out = {{3{1'b0}}, and_15_out};  // Bit_Extender bit_extender_21
  assign bit_extender_22_out = {{3{1'b0}}, and_16_out};  // Bit_Extender bit_extender_22
  assign bit_extender_23_out = {{3{1'b0}}, and_17_out};  // Bit_Extender bit_extender_23
  and and_22 (and_22_out, and_3_out, BrEq);
  and and_23 (and_23_out, and_4_out, not_2_out);
  and and_24 (and_24_out, and_5_out, BrLt);
  and and_25 (and_25_out, and_6_out, not_3_out);
  and and_26 (and_26_out, and_8_out, not_4_out);
  Comparator #(.width(7)) comparator_64 (.a(inst[31:25]), .b({7{1'b0}}), .eq(comparator_64_eq));  // open: gt, lt
  Comparator #(.width(7)) comparator_65 (.a(inst[31:25]), .b(7'b0000001), .eq(comparator_65_eq));  // open: gt, lt
  Comparator #(.width(7)) comparator_66 (.a(inst[31:25]), .b(7'b0100000), .eq(comparator_66_eq));  // open: gt, lt
  Multiplier #(.width(4)) multiplier_12 (
    .a(bit_extender_16_out), .b(4'b0010), .out(multiplier_12_out));  // open: cin, cout
  Multiplier #(.width(4)) multiplier_13 (
    .a(bit_extender_17_out), .b(4'b0001), .out(multiplier_13_out));  // open: cin, cout
  Comparator #(.width(7)) comparator_67 (.a(inst[31:25]), .b({7{1'b0}}), .eq(comparator_67_eq));  // open: gt, lt
  Comparator #(.width(7)) comparator_68 (.a(inst[31:25]), .b(7'b0100000), .eq(comparator_68_eq));  // open: gt, lt
  Multiplier #(.width(4)) multiplier_14 (
    .a(bit_extender_20_out), .b(4'b0000), .out(multiplier_14_out));  // open: cin, cout
  Multiplier #(.width(4)) multiplier_15 (
    .a(bit_extender_21_out), .b(4'b0110), .out(multiplier_15_out));  // open: cin, cout
  Multiplier #(.width(4)) multiplier_16 (
    .a(bit_extender_22_out), .b(4'b0111), .out(multiplier_16_out));  // open: cin, cout
  Multiplier #(.width(4)) multiplier_17 (
    .a(bit_extender_23_out), .b(4'b0011), .out(multiplier_17_out));  // open: cin, cout
  Multiplier #(.width(4)) multiplier_18 (
    .a(bit_extender_18_out), .b(4'b0010), .out(multiplier_18_out));  // open: cin, cout
  Multiplier #(.width(4)) multiplier_19 (
    .a(bit_extender_19_out), .b(4'b0001), .out(multiplier_19_out));  // open: cin, cout
  or or_4 (PCSel, and_22_out, and_23_out, and_24_out, and_25_out, and_21_out, and_26_out, comparator_35_eq, comparator_36_eq);
  and and_27 (and_27_out, comparator_52_eq, comparator_67_eq, comparator_57_eq);
  and and_28 (and_28_out, comparator_57_eq, comparator_68_eq, comparator_52_eq);
  Adder #(.width(4)) adder_13 (.a(adder_32_out), .b(multiplier_12_out), .out(adder_13_out));  // open: cin, cout
  Adder #(.width(4)) adder_14 (.a(adder_13_out), .b(multiplier_13_out), .out(adder_14_out));  // open: cin, cout
  assign bit_extender_24_out = {{3{1'b0}}, and_27_out};  // Bit_Extender bit_extender_24
  assign bit_extender_25_out = {{3{1'b0}}, and_28_out};  // Bit_Extender bit_extender_25
  and and_29 (and_29_out, comparator_64_eq, comparator_43_eq, comparator_49_eq);
  and and_30 (and_30_out, comparator_66_eq, comparator_43_eq, comparator_49_eq);
  and and_31 (and_31_out, comparator_64_eq, comparator_43_eq, comparator_44_eq);
  and and_32 (and_32_out, comparator_65_eq, comparator_43_eq, comparator_44_eq);
  and and_33 (and_33_out, comparator_66_eq, comparator_43_eq, comparator_44_eq);
  and and_34 (and_34_out, comparator_64_eq, comparator_43_eq, comparator_45_eq);
  and and_35 (and_35_out, comparator_65_eq, comparator_43_eq, comparator_45_eq);
  Adder #(.width(4)) adder_15 (.a(adder_14_out), .b(multiplier_14_out), .out(adder_15_out));  // open: cin, cout
  Adder #(.width(4)) adder_16 (.a(adder_15_out), .b(multiplier_15_out), .out(adder_16_out));  // open: cin, cout
  Adder #(.width(4)) adder_17 (.a(adder_16_out), .b(multiplier_16_out), .out(adder_17_out));  // open: cin, cout
  Adder #(.width(4)) adder_18 (.a(adder_17_out), .b(multiplier_17_out), .out(adder_18_out));  // open: cin, cout
  Adder #(.width(4)) adder_19 (.a(adder_23_out), .b(multiplier_18_out), .out(adder_19_out));  // open: cin, cout
  Adder #(.width(4)) adder_20 (.a(adder_19_out), .b(multiplier_19_out), .out(adder_20_out));  // open: cin, cout
  Adder #(.width(4)) adder_21 (.a(adder_20_out), .b(multiplier_11_out), .out(ALUSel));  // open: cin, cout
  assign bit_extender_26_out = {{3{1'b0}}, and_31_out};  // Bit_Extender bit_extender_26
  assign bit_extender_27_out = {{3{1'b0}}, and_32_out};  // Bit_Extender bit_extender_27
  assign bit_extender_28_out = {{3{1'b0}}, and_33_out};  // Bit_Extender bit_extender_28
  assign bit_extender_29_out = {{3{1'b0}}, and_34_out};  // Bit_Extender bit_extender_29
  assign bit_extender_30_out = {{3{1'b0}}, and_35_out};  // Bit_Extender bit_extender_30
  assign bit_extender_31_out = {{3{1'b0}}, and_9_out};  // Bit_Extender bit_extender_31
  assign bit_extender_32_out = {{3{1'b0}}, and_10_out};  // Bit_Extender bit_extender_32
  assign bit_extender_33_out = {{3{1'b0}}, and_11_out};  // Bit_Extender bit_extender_33
  assign bit_extender_34_out = {{3{1'b0}}, and_29_out};  // Bit_Extender bit_extender_34
  assign bit_extender_35_out = {{3{1'b0}}, and_30_out};  // Bit_Extender bit_extender_35
  Multiplier #(.width(4)) multiplier_20 (
    .a(bit_extender_24_out), .b(4'b0100), .out(multiplier_20_out));  // open: cin, cout
  Multiplier #(.width(4)) multiplier_21 (
    .a(bit_extender_25_out), .b(4'b0101), .out(multiplier_21_out));  // open: cin, cout
  Multiplier #(.width(4)) multiplier_22 (
    .a(bit_extender_26_out), .b(4'b0000), .out(multiplier_22_out));  // open: cin, cout
  Multiplier #(.width(4)) multiplier_23 (
    .a(bit_extender_27_out), .b(4'b1010), .out(multiplier_23_out));  // open: cin, cout
  Multiplier #(.width(4)) multiplier_24 (
    .a(bit_extender_28_out), .b(4'b1100), .out(multiplier_24_out));  // open: cin, cout
  Multiplier #(.width(4)) multiplier_25 (
    .a(bit_extender_29_out), .b(4'b0110), .out(multiplier_25_out));  // open: cin, cout
  Multiplier #(.width(4)) multiplier_26 (
    .a(bit_extender_30_out), .b(4'b1110), .out(multiplier_26_out));  // open: cin, cout
  Multiplier #(.width(4)) multiplier_27 (
    .a(bit_extender_31_out), .b(4'b0111), .out(multiplier_27_out));  // open: cin, cout
  Multiplier #(.width(4)) multiplier_28 (
    .a(bit_extender_32_out), .b(4'b1011), .out(multiplier_28_out));  // open: cin, cout
  Multiplier #(.width(4)) multiplier_29 (
    .a(bit_extender_33_out), .b(4'b0011), .out(multiplier_29_out));  // open: cin, cout
  Multiplier #(.width(4)) multiplier_30 (
    .a(bit_extender_34_out), .b(4'b0100), .out(multiplier_30_out));  // open: cin, cout
  Multiplier #(.width(4)) multiplier_31 (
    .a(bit_extender_35_out), .b(4'b0101), .out(multiplier_31_out));  // open: cin, cout
  Adder #(.width(4)) adder_22 (.a(adder_18_out), .b(multiplier_20_out), .out(adder_22_out));  // open: cin, cout
  Adder #(.width(4)) adder_23 (.a(adder_22_out), .b(multiplier_21_out), .out(adder_23_out));  // open: cin, cout
  Adder #(.width(4)) adder_24 (.a(multiplier_22_out), .b(multiplier_23_out), .out(adder_24_out));  // open: cin, cout
  Adder #(.width(4)) adder_25 (.a(adder_24_out), .b(multiplier_24_out), .out(adder_25_out));  // open: cin, cout
  Adder #(.width(4)) adder_26 (.a(adder_25_out), .b(multiplier_25_out), .out(adder_26_out));  // open: cin, cout
  Adder #(.width(4)) adder_27 (.a(adder_26_out), .b(multiplier_26_out), .out(adder_27_out));  // open: cin, cout
  Adder #(.width(4)) adder_28 (.a(adder_27_out), .b(multiplier_27_out), .out(adder_28_out));  // open: cin, cout
  Adder #(.width(4)) adder_29 (.a(adder_28_out), .b(multiplier_28_out), .out(adder_29_out));  // open: cin, cout
  Adder #(.width(4)) adder_30 (.a(adder_29_out), .b(multiplier_29_out), .out(adder_30_out));  // open: cin, cout
  Adder #(.width(4)) adder_31 (.a(adder_30_out), .b(multiplier_30_out), .out(adder_31_out));  // open: cin, cout
  Adder #(.width(4)) adder_32 (.a(adder_31_out), .b(multiplier_31_out), .out(adder_32_out));  // open: cin, cout

  // Other names for the same wires on the sheet: opcode[6:0] = inst[6:0]; funct3[2:0] = inst[14:12];
  //   imm_i[11:0] = inst[31:20]; funct7[6:0] = inst[31:25]

  // Notes on the sheet:
  //   INPUTS to your circuit
  //   I type
  //   R type
  //   R type
  //   I type
  //   I type
  //   I type
  //   I type
  //   U type
  //   U type
  //   UJ type
  //   SB type
  //   bltu
  //   bgeu
  //   S type
  //   R type
  //   R type
  //   I type
  //   I type
  //   U type
  //   U type
  //   SB type
  //   I type
  //   U type
  //   U type
  //   UJ type
  //   DON'T CHANGE THE LOCATIONS OF THE INPUTS AND OUTPUTS!
  //   OUTPUT from your circuit
  //   R type
  //   I type
  //   I type
  //   I type
  //   I type
  //   I type
  //   S type
  //   SB type
  //   U type
  //   U type
  //   UJ type
  //   SB type
  //   I type
  //   UJ type
  //   R type
  //   beq
  //   bne
  //   blt
  //   bge
  //   bltu
  //   bgeu
  //   slli
  //   CSR type
  //   CSR type
  //   addi
  //   slti
  //   xori
  //   ori
  //   andi
  //   csrwi type
  //   or
  //   and
  //   srli
  //   srai
  //   0
  //   1
  //   20
  //   R
  //   srl
  //   sra
  //   add
  //   mul
  //   sub
  //   sll
  //   mulh
  //   slt
  //   mulhu
  //   xor
endmodule
