// Logisim project cpu.circ as structural Verilog: 1 circuit, main circuit cpu
module cpu (
  input  clk,
  input  [31:0] INSTRUCTION,
  input  [31:0] READ_DATA,
  output [31:0] WRITE_ADDRESS,
  output [31:0] PROGRAM_COUNTER,
  output [31:0] ra,
  output [31:0] sp,
  output [31:0] t0,
  output [31:0] t1,
  output [31:0] t2,
  output [31:0] s0,
  output [31:0] s1,
  output [31:0] a0,
  output [31:0] tohost,
  output [3:0] WRITE_ENABLE,
  output [31:0] WRITE_DATA
);

  wire ASel, BrEq, BrLt, BrUn, BSel, CSRSel, CSRWen, MemRW, PCSEL, RegWEn;
  wire [1:0] WBSel;
  wire [2:0] funct3, ImmSel;
  wire [3:0] ALUSel, bit_extender_5_out, mask, multiplexer_6_out;
  wire [4:0] bit_extender_3_out, bit_extender_4_out, multiplier_1_out, multiplier_2_out, rd, rs1, rs2;
  wire [6:0] funct7, opcode;
  wire [11:0] bit_extender_2_out;
  wire [31:0] adder_1_out, adder_2_out, bit_extender_1_out, bit_extender_6_out, bit_extender_7_out,
       imm_result, multiplexer_1_out, multiplexer_2_out, multiplexer_3_out, multiplexer_4_out,
       multiplexer_5_out, pc_plusfour, Read_Data_1, READ_DATA_2, Read_Data_2_t, READ_FINAL, READ_NEW,
       register_2_q, WRITEBACK;

  assign bit_extender_1_out = {{27{1'b0}}, rs1};  // Bit_Extender bit_extender_1
  Multiplexer #(.enable("false"), .width(32)) multiplexer_1 (
    .in0(Read_Data_1), .in1(bit_extender_1_out), .out(multiplexer_1_out), .sel(CSRSel));
  Multiplexer #(.enable("false"), .width(32)) multiplexer_2 (
    .in0(adder_1_out), .in1(WRITE_ADDRESS), .out(multiplexer_2_out), .sel(PCSEL));
  Multiplexer #(.enable("false"), .width(32)) multiplexer_3 (
    .in0(INSTRUCTION), .in1(32'h13), .out(multiplexer_3_out), .sel(PCSEL));
  Bit_Extender #(.in_width(32), .out_width(12)) bit_extender_2 (.in(imm_result), .out(bit_extender_2_out));
  Register #(.width(32)) PC (.D(multiplexer_2_out), .en(1'b1), .clk(clk), .Q(PROGRAM_COUNTER));  // open: clr
  Adder #(.width(32)) adder_1 (.a(PROGRAM_COUNTER), .b(32'h4), .out(adder_1_out));  // open: cin, cout
  Register #(.width(32)) register_1 (
    .D(multiplexer_3_out), .en(1'b1), .clk(clk), .Q({funct7, rs2, rs1, funct3, rd, opcode}));  // open: clr
  control_logic control_logic_1 (
    .CSRWen(CSRWen), .PCSel(PCSEL), .RegWEn(RegWEn), .ImmSel(ImmSel), .BrUn(BrUn), .ASel(ASel), .BSel(BSel),
    .ALUSel(ALUSel), .MemRW(MemRW), .WBSel(WBSel), .CSRSel(CSRSel),
    .inst({funct7, rs2, rs1, funct3, rd, opcode}), .BrEq(BrEq), .BrLt(BrLt));
  csr csr_1 (
    .CSR_address(bit_extender_2_out), .CSR_din(multiplexer_1_out), .CSR_WE(CSRWen), .clk(clk), .tohost(tohost));
  Register #(.width(32)) register_2 (.D(INSTRUCTION), .en(1'b1), .clk(clk), .Q(register_2_q));  // open: clr
  regfile regfile_1 (
    .rs1(rs1), .rs2(rs2), .rd(rd), .Write_Data(WRITEBACK), .RegWEn(RegWEn), .clk(clk), .ra(ra), .sp(sp),
    .t0(t0), .t1(t1), .t2(t2), .s0(s0), .s1(s1), .a0(a0), .Read_Data_1(Read_Data_1),
    .Read_Data_2(Read_Data_2_t));
  imm_gen imm_gen_1 (.inst(register_2_q), .ImmSel(ImmSel), .imm(imm_result));
  Multiplexer #(.enable("false"), .width(32)) multiplexer_4 (
    .in0(Read_Data_1), .in1(pc_plusfour), .out(multiplexer_4_out), .sel(ASel));
  Multiplexer #(.enable("false"), .width(32)) multiplexer_5 (
    .in0(Read_Data_2_t), .in1(imm_result), .out(multiplexer_5_out), .sel(BSel));
  branch_comp branch_comp_1 (.rs1(Read_Data_1), .rs2(Read_Data_2_t), .BrUn(BrUn), .BrEq(BrEq), .BrLt(BrLt));
  alu alu_1 (.Result(WRITE_ADDRESS), .A(multiplexer_4_out), .B(multiplexer_5_out), .ALUSel(ALUSel));
  Multiplexer #(.enable("false"), .select(3), .width(4)) multiplexer_6 (
    .in0(4'b0001), .in1(4'b0011), .in2(4'b1111), .out(multiplexer_6_out), .sel(funct3));  // open: in3, in4, in5, in6, in7
  Register #(.width(32)) register_3 (.D(PROGRAM_COUNTER), .en(1'b1), .clk(clk), .Q(pc_plusfour));  // open: clr
  Shifter #(.width(4)) shifter_1 (.in(multiplexer_6_out), .\dist (imm_result[1:0]), .out(mask));
  Adder #(.width(32)) adder_2 (.a(pc_plusfour), .b(32'h4), .out(adder_2_out));  // open: cin, cout
  assign bit_extender_3_out = {{3{1'b0}}, imm_result[1:0]};  // Bit_Extender bit_extender_3
  assign bit_extender_4_out = {{3{1'b0}}, imm_result[1:0]};  // Bit_Extender bit_extender_4
  Multiplexer #(.enable("false"), .select(2), .width(32)) multiplexer_7 (
    .in0(adder_2_out), .in1(WRITE_ADDRESS), .in2(READ_FINAL), .out(WRITEBACK), .sel(WBSel));  // open: in3
  assign bit_extender_5_out = {{3{1'b0}}, MemRW};  // Bit_Extender bit_extender_5
  assign WRITE_ENABLE = bit_extender_5_out & mask;  // AND_Gate and_1, 4 bits wide
  Shifter #(.shift("ar"), .width(32)) shifter_2 (.in(READ_DATA), .\dist (multiplier_1_out), .out(READ_NEW));
  Multiplier #(.width(5)) multiplier_1 (
    .a(bit_extender_3_out), .b(5'b01000), .out(multiplier_1_out));  // open: cin, cout
  Shifter #(.width(32)) shifter_3 (.in(READ_DATA_2), .\dist (multiplier_2_out), .out(WRITE_DATA));
  Multiplier #(.width(5)) multiplier_2 (
    .a(bit_extender_4_out), .b(5'b01000), .out(multiplier_2_out));  // open: cin, cout
  assign bit_extender_6_out = {{16{READ_NEW[15]}}, READ_NEW[15:0]};  // Bit_Extender bit_extender_6
  Multiplexer #(.enable("false"), .select(3), .width(32)) multiplexer_8 (
    .in0(bit_extender_7_out), .in1(bit_extender_6_out), .in2(READ_NEW), .out(READ_FINAL), .sel(funct3));  // open: in3, in4, in5, in6, in7
  assign bit_extender_7_out = {{24{READ_NEW[7]}}, READ_NEW[7:0]};  // Bit_Extender bit_extender_7

  // Other names for the same wires on the sheet: pc_tunnel[31:0] = PROGRAM_COUNTER

  // Notes on the sheet:
  //   Output to IMEM
  //   IMEM (do **NOT** move this)
  //   PC+4
  //   ALU
  //   Inputs from IMEM
  //   PC+4
  //   It is OK to move the PC, RegFile, ALU, MEM, Branch Comp, Imm Gen, and Control Logic to wherever is most convenient for you when constructing your CPU, and to delete this text
  //   Inputs/Outputs for testing. Do **NOT** move these.
  //   Outputs To DMEM
  //   DMEM (do **NOT** move this)
  //   Inputs From DMEM
endmodule
