// Logisim project imm_gen.circ as structural Verilog: 1 circuit, main circuit imm_gen
module imm_gen (
  input  [31:0] inst,
  input  [2:0] ImmSel,
  output [31:0] imm
);

  wire [11:0] demultiplexer_1_out5;
  wire [20:0] bit_extender_1_out;
  wire [31:0] bit_extender_2_out, demultiplexer_1_out2, demultiplexer_1_out3, demultiplexer_1_out4,
       demultiplexer_1_out6;
  wire [31:1] demultiplexer_1_out4_2, demultiplexer_1_out6_2;
  wire [31:12] demultiplexer_1_out5_2;

  Demultiplexer #(.enable("false"), .select(3), .width(32)) demultiplexer_1 (
    .out2(demultiplexer_1_out2), .out3(demultiplexer_1_out3),
    .out4({demultiplexer_1_out4[31], demultiplexer_1_out4_2[10:5], demultiplexer_1_out4[24:12], demultiplexer_1_out4_2[4:1], demultiplexer_1_out4_2[11], demultiplexer_1_out4[6:0]}),
    .out5({demultiplexer_1_out5_2, demultiplexer_1_out5}),
    .out6({demultiplexer_1_out6[31], demultiplexer_1_out6_2[10:1], demultiplexer_1_out6_2[11], demultiplexer_1_out6_2[19:12], demultiplexer_1_out6[11:0]}),
    .in(inst), .sel(ImmSel));  // open: out0, out1, out7
  assign bit_extender_1_out = {{20{demultiplexer_1_out3[31]}}, demultiplexer_1_out3[31]};  // Bit_Extender bit_extender_1
  assign bit_extender_2_out = {{20{demultiplexer_1_out2[31]}}, demultiplexer_1_out2[31:20]};  // Bit_Extender bit_extender_2
  assign demultiplexer_1_out4_2[31:12] = {{19{demultiplexer_1_out4[31]}}, demultiplexer_1_out4[31]};  // Bit_Extender bit_extender_3
  assign demultiplexer_1_out6_2[31:20] = {{11{demultiplexer_1_out6[31]}}, demultiplexer_1_out6[31]};  // Bit_Extender bit_extender_4
  Multiplexer #(.enable("false"), .select(3), .width(32)) multiplexer_1 (
    .in2(bit_extender_2_out),
    .in3({bit_extender_1_out, demultiplexer_1_out3[30:25], demultiplexer_1_out3[11:7]}),
    .in4({demultiplexer_1_out4_2, 1'b0}), .in5({demultiplexer_1_out5_2, {12{1'b0}}}),
    .in6({demultiplexer_1_out6_2, 1'b0}), .out(imm), .sel(ImmSel));  // open: in0, in1, in7

  // Notes on the sheet:
  //   INPUTS to your circuit
  //   DON'T CHANGE THE LOCATIONS OF THE INPUTS AND OUTPUTS!
  //   I type
  //   S type
  //   UJ type
  //   SB type
  //   U type
  //   OUTPUT from your circuit
endmodule
